// Logisim project Advanced_computer.circ as structural Verilog
module PC_counter (
  input  in_1,
  input  [15:0] in_2,
  input  in_3,
  input  in_4,
  output [15:0] out_5
);

  Counter #(.max('hffff), .width(16)) counter_1 (
    .load(in_1), .D(in_2), .count(1'b1), .Q(out_5), .up(1'b1), .clk(in_3), .clr(in_4));  // open: carry
endmodule
